# Fritzing sketch NoSTM32 (saved by Fritzing 0.9.3b)
circuit board: 7.01282cm x 6.5448cm
breadboards: 1

parts:
  BerryGPS = double row male pin header, 8 pins [form="♂ (male)"]
  M1 = STM32F103C8T6 blue mini board

nets:
  N1: BerryGPS.pin1, M1.3.3V
  N2: BerryGPS.pin2, M1.B11
  N3: BerryGPS.pin3, M1.B10
  N4: BerryGPS.pin5, M1.A9
  N5: BerryGPS.pin6, M1.A10
  N6: BerryGPS.pin7, M1.G
  N7: BerryGPS.pin8, M1.B12

notes:
  3.3V
  5V
  SDA
  SCL
  GND
  GPS_RX
  GPS_TX
  Kevin Lieng
